// Digital circuit computer.dig as structural Verilog
module computer (
  input  clk,
  input  Clock_Enable,
  input  [15:0] Data_Bus_Manual_Input,
  input  Manual_Clock_Tick,
  input  in_5,
  input  in_6,
  input  in_7,
  input  in_8,
  input  [2:0] in_9,
  input  in_10,
  input  in_11,
  input  in_12,
  input  in_13,
  input  in_14,
  input  in_15,
  input  Data_bus_manual_override,
  input  in_17,
  input  in_18,
  input  in_19
);

  wire ALUn, ALUo, ALUz, Clock, driverinvsel_3_out, not_1_out;
  wire [2:0] counter_1_out;
  wire [9:0] add_1_s, driverinvsel_2_out, Memory_Address_Register_q, Program_Counter_q;
  wire [15:0] alu_1_y, Instruction_Register_q, RAM_d, Register_A_q, Register_B_q;

  assign Clock = ~Clock_Enable ? Manual_Clock_Tick : 1'bz;  // DriverInvSel driverinvsel_1
  assign Clock = Clock_Enable ? clk : 1'bz;  // Driver driver_1
  assign driverinvsel_2_out = ~in_17 ? RAM_d[9:0] : 10'bz;  // DriverInvSel driverinvsel_2
  assign driverinvsel_2_out = in_17 ? add_1_s : 10'bz;  // Driver driver_2
  LED led_1 (.in(Clock_Enable));
  Register #(.Bits(10)) Memory_Address_Register (.D(RAM_d[9:0]), .C(Clock), .en(in_13), .Q(Memory_Address_Register_q));
  Register #(.Bits(10), .isProgramCounter("true")) Program_Counter (
    .D(driverinvsel_2_out), .C(Clock), .en(driverinvsel_3_out), .Q(Program_Counter_q));
  assign driverinvsel_3_out = ~in_17 ? in_14 : 1'bz;  // DriverInvSel driverinvsel_3
  assign driverinvsel_3_out = in_17 ? 1'b1 : 1'bz;  // Driver driver_3
  Add #(.Bits(10)) add_1 (.a(10'h1), .b(Program_Counter_q), .c_i(1'b0), .s(add_1_s));  // open: c_o
  RAMDualPort #(.AddrBits(10), .Bits(16)) RAM (
    .A(Memory_Address_Register_q), .Din(RAM_d), .str(in_11), .C(Clock), .ld(in_12), .D(RAM_d));
  ROM #(.AddrBits(10), .Bits(16), .isProgramMemory("true")) ROM (.A(Program_Counter_q), .sel(in_15), .D(RAM_d));
  not not_1 (not_1_out, Clock);
  assign RAM_d = Data_bus_manual_override ? Data_Bus_Manual_Input : 16'bz;  // Driver driver_4
  assign RAM_d = in_5 ? Register_A_q : 16'bz;  // Driver driver_5
  assign RAM_d = in_10 ? alu_1_y : 16'bz;  // Driver driver_6
  assign RAM_d = in_7 ? Register_B_q : 16'bz;  // Driver driver_7
  Register #(.Bits(16)) Instruction_Register (.D(RAM_d), .C(Clock), .en(in_18), .Q(Instruction_Register_q));
  Counter #(.Bits(3)) counter_1 (.en(1'b1), .C(not_1_out), .clr(in_19), .out(counter_1_out));  // open: ovf
  Register #(.Bits(16)) Register_A (.D(RAM_d), .C(Clock), .en(in_6), .Q(Register_A_q));
  Register #(.Bits(16)) Register_B (.D(RAM_d), .C(Clock), .en(in_8), .Q(Register_B_q));
  ALU alu_1 (.A(Register_A_q), .B(Register_B_q), .Op(in_9), .Ci(1'b0), .Y(alu_1_y), .O(ALUo), .Z(ALUz), .N(ALUn));
  ROM #(.AddrBits(9), .Bits(13)) rom_2 (.A({counter_1_out, Instruction_Register_q[5:0]}), .sel(1'b1));  // open: D

  // Other names for the same wires on the sheet: ALUop[2:0] = in_9; ALUre = in_10; IRwr = in_18; MARwr = in_13;
  //   PCin = in_17; PCwr = in_14; RAMre = in_12; RAMwr = in_11; RAre = in_5; RAwr = in_6; RBre = in_7; RBwr = in_8;
  //   ROMre = in_15; SCclr = in_19

  // Notes on the sheet:
  //   contents of ROM (hex, n*v repeats v):
  //   6,4,2
endmodule
